# Fritzing sketch modelo (saved by Fritzing 0.9.3b)
breadboards: 1

parts:
  Componente1 = Arduino Uno (Rev3)
  J1 = Piezo Speaker
  LCD1 = LCD screen  # not connected
  LCM1602_IIC1 = LCM1602 IIC [part_number="LCM1602 IIC" chip_label="LCM1602 IIC" package="DIP (Dual Inline) [THT]"]
  LED1 = LED - 5mm [color="Red (633nm)" package="5 mm [THT]"]
  Componente2 = sensor_biometrico
  Part2 = Bluetooth HC-05 Macho
  S1 = Pushbutton [package="[THT]"]

nets:
  N1: Componente1.A4/SDA, LCM1602_IIC1.SDA
  N2: Componente1.A5/SCL, LCM1602_IIC1.SCL
  N3: Componente1.D0/RX, Part2.TXD
  N4: Componente1.D1/TX, Part2.RXD
  N5: Componente1.D3_PWM, Componente2.RX
  N6: Componente1.D4, Componente2.TX
  N7: Componente1.D5_PWM, J1.pin2
  N8: Componente1.D6_PWM, LED1.cathode
  N9: Componente1.RESET, S1.Pin_3, S1.Pin_4
  3V3: Componente1.3V3, Componente2.VCC
  VCC: Componente1.5V, J1.pin1, LCM1602_IIC1.VCC, Part2.VCC
  GND: Componente1.GND, LCM1602_IIC1.GND, LED1.anode, Componente2.GND, Part2.GND

custom parts:
  LCM1602 IIC: I2C-Module to use a 1602 or 2004 LCD on with the wire.h libory Serial LCD Modul
  sensor_biometrico: Adafruit Optical Fingerprint Sensor
